// Logisim project A(B+C)+A`B.circ as structural Verilog: 1 circuit, main circuit main
module main (
  input  in_1,
  input  in_2,
  input  in_3,
  input  in_4,
  output out_5
);

  wire and_1_out, and_2_out, not_1_out, or_1_out;

  or or_1 (or_1_out, in_1, in_2);
  not not_1 (not_1_out, in_3);
  and and_1 (and_1_out, not_1_out, not_1_out, in_4);
  and and_2 (and_2_out, or_1_out, in_3, in_3);
  or or_2 (out_5, and_2_out, and_1_out);
endmodule
