// Logisim project 1,2,4 FULL ADDER.circ as structural Verilog: 1 circuit, main circuit main
module main (
  input  in_1,
  input  A3,
  input  A2,
  input  A1,
  input  A0,
  input  [1:0] in_6,
  input  [1:0] in_7,
  input  in_8,
  input  [1:0] in_9,
  input  [1:0] in_10,
  input  in_11,
  input  [3:0] in_12,
  input  [3:0] in_13,
  input  B3,
  input  B2,
  input  B1,
  input  B0,
  output [1:0] out_18,
  output [1:0] out_19,
  output out_20,
  output [3:0] out_21,
  output out_22,
  output out_23
);

  wire adder_1_cout, adder_4_cout, adder_4_out, adder_5_cout, adder_5_out, adder_6_cout, adder_6_out,
       adder_7_out;

  Adder #(.width(2)) adder_1 (.a(in_6), .b(in_10), .out(out_19), .cin(in_1), .cout(adder_1_cout));
  Adder #(.width(2)) adder_2 (.a(in_7), .b(in_9), .out(out_18), .cin(adder_1_cout), .cout(out_20));
  Adder #(.width(4)) adder_3 (.a(in_12), .b(in_13), .out(out_21), .cin(in_11), .cout(out_23));
  Adder #(.width(1)) adder_4 (.a(A0), .b(B0), .out(adder_4_out), .cin(in_8), .cout(adder_4_cout));
  Adder #(.width(1)) adder_5 (.a(A1), .b(B1), .out(adder_5_out), .cin(adder_4_cout), .cout(adder_5_cout));
  Adder #(.width(1)) adder_6 (.a(A2), .b(B2), .out(adder_6_out), .cin(adder_5_cout), .cout(adder_6_cout));
  Adder #(.width(1)) adder_7 (.a(A3), .b(B3), .out(adder_7_out), .cin(adder_6_cout), .cout(out_22));
  LED led_1 (.in(adder_7_out));
  LED led_2 (.in(adder_4_out));
  LED led_3 (.in(adder_6_out));
  LED led_4 (.in(adder_5_out));
endmodule
