// Logisim project 4 1 Full Adder.circ as structural Verilog: 1 circuit, main circuit main
module main (
  input  A3,
  input  A2,
  input  A1,
  input  A0,
  input  in_5,
  input  B3,
  input  B2,
  input  B1,
  input  B0,
  output out_10
);

  wire adder_1_cout, adder_1_out, adder_2_cout, adder_2_out, adder_3_cout, adder_3_out, adder_4_out;

  Adder #(.width(1)) adder_1 (.a(A0), .b(B0), .out(adder_1_out), .cin(in_5), .cout(adder_1_cout));
  Adder #(.width(1)) adder_2 (.a(A1), .b(B1), .out(adder_2_out), .cin(adder_1_cout), .cout(adder_2_cout));
  Adder #(.width(1)) adder_3 (.a(A2), .b(B2), .out(adder_3_out), .cin(adder_2_cout), .cout(adder_3_cout));
  Adder #(.width(1)) adder_4 (.a(A3), .b(B3), .out(adder_4_out), .cin(adder_3_cout), .cout(out_10));
  LED led_1 (.in(adder_3_out));
  LED led_2 (.in(adder_4_out));
  LED led_3 (.in(adder_2_out));
  LED led_4 (.in(adder_1_out));
endmodule
