// Logisim project 3-to-8 line hierarchical decoder.circ as structural Verilog: 1 circuit, main circuit main
module main (
  input  [1:0] in_1,
  input  in_2,
  output out_3,
  output out_4,
  output out_5,
  output out_6,
  output out_7,
  output out_8,
  output out_9,
  output out_10
);

  wire decoder_1_out0, decoder_1_out1, decoder_1_out2, decoder_1_out3, decoder_2_out0, decoder_2_out1;

  Decoder #(.select(2)) decoder_1 (
    .out0(decoder_1_out0), .out1(decoder_1_out1), .out2(decoder_1_out2), .out3(decoder_1_out3), .sel(in_1));  // open: en
  Decoder decoder_2 (.out0(decoder_2_out0), .out1(decoder_2_out1), .sel(in_2));  // open: en
  and and_1 (out_3, decoder_1_out0, decoder_2_out0);
  and and_2 (out_4, decoder_1_out0, decoder_2_out1);
  and and_3 (out_5, decoder_1_out1, decoder_2_out0);
  and and_4 (out_6, decoder_1_out1, decoder_2_out1);
  and and_5 (out_7, decoder_1_out2, decoder_2_out0);
  and and_6 (out_8, decoder_1_out2, decoder_2_out1);
  and and_7 (out_9, decoder_1_out3, decoder_2_out0);
  and and_8 (out_10, decoder_1_out3, decoder_2_out1);
endmodule
