// Logisim project 2-1 bit.circ as structural Verilog: 1 circuit, main circuit main
module main (
  input  I7,
  input  I6,
  input  I5,
  input  I4,
  input  I3,
  input  I2,
  input  I1,
  input  I0,
  input  A,
  input  B,
  input  C,
  output out_12
);

  wire multiplexer_1_out, multiplexer_2_out, multiplexer_3_out, multiplexer_4_out, multiplexer_5_out,
       multiplexer_6_out;

  Multiplexer multiplexer_1 (.in0(I0), .in1(I1), .out(multiplexer_1_out), .sel(C));  // open: en
  Multiplexer multiplexer_2 (.in0(I2), .in1(I3), .out(multiplexer_2_out), .sel(C));  // open: en
  Multiplexer multiplexer_3 (.in0(I4), .in1(I5), .out(multiplexer_3_out), .sel(C));  // open: en
  Multiplexer multiplexer_4 (.in0(I6), .in1(I7), .out(multiplexer_4_out), .sel(C));  // open: en
  Multiplexer multiplexer_5 (
    .in0(multiplexer_1_out), .in1(multiplexer_2_out), .out(multiplexer_5_out), .sel(B));  // open: en
  Multiplexer multiplexer_6 (
    .in0(multiplexer_3_out), .in1(multiplexer_4_out), .out(multiplexer_6_out), .sel(B));  // open: en
  Multiplexer multiplexer_7 (.in0(multiplexer_5_out), .in1(multiplexer_6_out), .out(out_12), .sel(A));  // open: en
endmodule
