// Logisim project 4-1 bit(1,3,6,7).circ as structural Verilog: 1 circuit, main circuit main
module main (
  input  A,
  input  B,
  input  [1:0] X_Y,
  input  C,
  output out_5
);

  wire not_1_out;

  not not_1 (not_1_out, C);
  Multiplexer #(.select(2)) multiplexer_1 (.in0(C), .in1(C), .in2(B), .in3(A), .out(out_5), .sel(X_Y));  // open: en
endmodule
