// Logisim project 8-1 bit(0,2,5,7).circ as structural Verilog: 1 circuit, main circuit main
module main (
  input  B,
  input  A,
  input  [2:0] A_B_C,
  output OUTPUT
);

  Multiplexer #(.select(3)) multiplexer_1 (
    .in0(A), .in1(B), .in2(A), .in3(B), .in4(B), .in5(A), .in6(B), .in7(A), .out(OUTPUT), .sel(A_B_C));  // open: en
endmodule
