// Logisim project register.circ as structural Verilog: 1 circuit, main circuit main
module main (
  input  in_1,
  input  in_2,
  input  in_3,
  input  in_4,
  input  in_5,
  input  in_6
);

  wire clock_1_out, clock_2_out, clock_3_out, d_ff_1_q, d_ff_1_qn, register_1_q, register_2_q, register_3_q,
       register_4_q;

  Clock clock_1 (.out(clock_1_out));
  D_Flip_Flop d_ff_1 (.clk(clock_1_out), .D(in_3), .Q(d_ff_1_q), .Qn(d_ff_1_qn), .en(in_4));  // open: preset, reset
  LED led_1 (.in(d_ff_1_q));
  LED led_2 (.in(d_ff_1_qn));
  Clock clock_2 (.out(clock_2_out));
  Clock clock_3 (.out(clock_3_out));
  LED led_3 (.in(register_1_q));
  Register #(.width(1)) register_1 (.D(register_4_q), .en(in_2), .Q(register_1_q), .clk(clock_3_out));  // open: clr
  Register #(.width(1)) register_2 (.D(in_5), .en(in_6), .Q(register_2_q), .clk(clock_2_out));  // open: clr
  Register #(.width(1)) register_3 (.D(register_2_q), .en(in_6), .Q(register_3_q), .clk(clock_2_out));  // open: clr
  Register #(.width(1)) register_4 (.D(in_1), .en(in_2), .Q(register_4_q), .clk(clock_3_out));  // open: clr
  LED led_4 (.in(register_3_q));
endmodule
